# Fritzing sketch PCB (saved by Fritzing 0.9.0b)
circuit board: 5.5cm x 6.5cm
breadboards: 1

parts:
  U1 = 74HC165 [part_number=SN74LS165 package="DIP16 [THT]"]
  R1 = Resistor [tolerance=±5% resistance=220 package=THT]
  R2 = Resistor [tolerance=±5% resistance=220 package=THT]
  R3 = Resistor [tolerance=±5% resistance=220 package=THT]
  R4 = Resistor [tolerance=±5% resistance=220 package=THT]
  R5 = Resistor [tolerance=±5% resistance=220 package=THT]
  R6 = Resistor [tolerance=±5% resistance=220 package=THT]
  R7 = Resistor [tolerance=±5% resistance=220 package=THT]
  R8 = Resistor [tolerance=±5% resistance=220 package=THT]
  Part1 = Arduino Pro Mini v13
  U2 = 74HC595 [package="DIP16 [THT]"]
  R9 = Resistor [tolerance=±5% resistance=220 package=THT]
  R10 = Resistor [tolerance=±5% resistance=220 package=THT]
  J1 = Piezo Speaker
  RHT1 = Humidity and Temperature Sensor RHT03
  RHT2 = Humidity and Temperature Sensor RHT03
  RHT3 = Humidity and Temperature Sensor RHT03
  RHT4 = Humidity and Temperature Sensor RHT03
  RHT5 = Humidity and Temperature Sensor RHT03
  RHT6 = Humidity and Temperature Sensor RHT03
  RHT7 = Humidity and Temperature Sensor RHT03
  RHT8 = Humidity and Temperature Sensor RHT03
  RHT9 = Humidity and Temperature Sensor RHT03
  RHT10 = Humidity and Temperature Sensor RHT03  # not connected
  RHT11 = Humidity and Temperature Sensor RHT03  # not connected

nets:
  N1: U1.Q1, Part1.D11_PWM/MOSI
  N2: U1.Q2, Part1.D10_PWM/SS
  N3: U1.Q3, R5.Pin_1
  N4: U1.Q4, R6.Pin_1
  N5: U1.Q5, R7.Pin_1
  N6: U1.Q6, R8.Pin_1
  GND: U1.GND, U1.MR, U1.Q0, Part1.GND, U2.GND, R10.Pin_0, J1.pin1, RHT1.GND_2
  N7: U1.Q7', Part1.D12/MISO, R9.Pin_0
  N8: U1.SH_CP, R1.Pin_0
  N9: U1.ST_CP, R2.Pin_0
  N10: U1.OE, R3.Pin_0
  N11: U1.DS, R4.Pin_0
  VCC: U1.VCC, Part1.VCC, U2.MR, U2.VCC, RHT1.GND_1
  N12: Part1.D0/TX, RHT1.Vcc
  N13: Part1.D1/RX, RHT1.Data-signal
  VCC_2: Part1.A3, RHT7.Vcc, RHT9.Vcc
  N14: Part1.A2, RHT7.Data-signal, RHT9.Data-signal
  N15: Part1.A1, RHT7.GND_1, RHT9.GND_1
  N16: Part1.A0, RHT7.GND_2, RHT9.GND_2
  N17: Part1.D13/SCK, J1.pin2
  N18: Part1.D9_PWM, U2.DS
  N19: Part1.D8, U2.ST_CP
  N20: Part1.D7, U2.SH_CP
  N21: R9.Pin_1, R10.Pin_1
  VCC_3: RHT2.Vcc, RHT4.Vcc
  N22: RHT2.Data-signal, RHT4.Data-signal
  N23: RHT2.GND_1, RHT4.GND_1
  N24: RHT2.GND_2, RHT4.GND_2
  VCC_4: RHT3.Vcc, RHT5.Vcc
  N25: RHT3.Data-signal, RHT5.Data-signal
  N26: RHT3.GND_1, RHT5.GND_1
  N27: RHT3.GND_2, RHT5.GND_2
  VCC_5: RHT6.Vcc, RHT8.Vcc
  N28: RHT6.Data-signal, RHT8.Data-signal
  N29: RHT6.GND_1, RHT8.GND_1
  N30: RHT6.GND_2, RHT8.GND_2

custom parts:
  74HC165: 8-bit parallel-load shift registers
